# Fritzing sketch jcscpu-hmc_ram (saved by Fritzing 0.9.4)
breadboards: 7

parts:
  Part1 = Arduino Nano (Rev3.0) (ICSP)
  R1 = Resistor [tolerance=±5% resistance=10k package=THT]
  R2 = Resistor [tolerance=±5% resistance=10k package=THT]
  R3 = Resistor [tolerance=±5% resistance=10k package=THT]
  R5 = Resistor [tolerance=±5% resistance=10k package=THT]

nets:
  N1: Part1.D2, R5.Pin_0
  N2: Part1.D3, R3.Pin_0
  N3: Part1.D4, R1.Pin_0
  N4: Part1.A3, R2.Pin_0
  N5: R1.Pin_1, R2.Pin_1, R3.Pin_1, R5.Pin_1

notes:
  HLT
  MAR_s
  RAM_e
  RAM_s
  R1_s
