# Fritzing sketch jcscpu-hmc_alu (saved by Fritzing 0.9.4)
breadboards: 7

parts:
  Part1 = Arduino Nano (Rev3.0) (ICSP)
  Part2 = Arduino Nano (Rev3.0) (ICSP)
  R1 = Resistor [tolerance=±5% resistance=10k package=THT]
  R2 = Resistor [tolerance=±5% resistance=10k package=THT]
  R3 = Resistor [tolerance=±5% resistance=10k package=THT]
  R4 = Resistor [tolerance=±5% resistance=10k package=THT]
  R5 = Resistor [tolerance=±5% resistance=10k package=THT]
  R6 = Resistor [tolerance=±5% resistance=10k package=THT]
  R7 = Resistor [tolerance=±5% resistance=10k package=THT]
  R8 = Resistor [tolerance=±5% resistance=10k package=THT]
  LED97 = LED - 3mm [color="Blue (505nm)" package="3 mm [THT]"]
  LED98 = LED - 3mm [color="Blue (505nm)" package="3 mm [THT]"]
  LED99 = LED - 3mm [color="Blue (505nm)" package="3 mm [THT]"]
  LED100 = LED - 3mm [color="Blue (505nm)" package="3 mm [THT]"]
  R82 = Resistor [tolerance=±5% resistance=1k package=THT]
  R83 = Resistor [tolerance=±5% resistance=1k package=THT]
  R85 = Resistor [tolerance=±5% resistance=1k package=THT]
  R86 = Resistor [tolerance=±5% resistance=1k package=THT]

nets:
  N1: Part1.A5, Part2.A5
  N2: Part1.A4, Part2.A4
  N3: Part2.GND, R1.Pin_1, R2.Pin_1, R3.Pin_1, R4.Pin_1, R5.Pin_1, R6.Pin_1, R7.Pin_1, R8.Pin_1
  N4: Part2.D2, R6.Pin_0
  N5: Part2.D5, R5.Pin_0
  N6: Part2.D6, R7.Pin_0
  N7: Part2.D7, R4.Pin_0
  N8: Part2.D8, R8.Pin_0
  N9: Part2.D9, LED98.anode
  N10: Part2.D10, LED99.anode
  N11: Part2.D11/MOSI, LED97.anode
  N12: Part2.D12/MISO, LED100.anode
  N13: Part2.A2, R3.Pin_0
  N14: Part2.A1, R2.Pin_0
  N15: Part2.A0, R1.Pin_0
  N16: LED97.cathode, R82.Pin_1
  N17: LED98.cathode, R83.Pin_1
  N18: LED99.cathode, R86.Pin_1
  N19: LED100.cathode, R85.Pin_1
  N20: R82.Pin_0, R83.Pin_0, R85.Pin_0, R86.Pin_0

notes:
  ALU2
  ALU1
  ALU0
  TMP_s
  ACC_e
  BUS1
  ACC_s
  R1_s
  C     A     E     Z
  CARRY IN
