# Fritzing sketch jcscpu-hmc_r0r1_bb (saved by Fritzing 0.9.4)
breadboards: 14

parts:
  Part1 = Arduino Nano (Rev3.0) (ICSP)
  Part2 = Arduino Nano (Rev3.0) (ICSP)
  Part3 = Arduino Nano (Rev3.0) (ICSP)
  SN74HC376 = IC, DIP package, 20 pins [chip_label=SN74HC373]
  SN74HC381 = IC, DIP package, 20 pins [chip_label=SN74HC373]
  SN74HC384 = IC, DIP package, 14 pins [chip_label=SN74HC00]
  R93 = Resistor [tolerance=±5% resistance=10k package="0402 [SMD]"]
  R94 = Resistor [tolerance=±5% resistance=10k package="0402 [SMD]"]
  R95 = Resistor [tolerance=±5% resistance=10k package="0402 [SMD]"]
  R96 = Resistor [tolerance=±5% resistance=10k package="0402 [SMD]"]

nets:
  N1: Part1.A5, Part2.A5, Part3.A5
  N2: Part1.A4, Part2.A4, Part3.A4
  N3: Part3.GND, SN74HC384.pin7
  N4: SN74HC376.pin1, SN74HC384.pin6
  N5: SN74HC376.pin2, SN74HC376.pin3, SN74HC381.pin2, SN74HC381.pin3
  N6: SN74HC376.pin4, SN74HC376.pin5, SN74HC381.pin4, SN74HC381.pin5
  N7: SN74HC376.pin6, SN74HC376.pin7, SN74HC381.pin6, SN74HC381.pin7
  N8: SN74HC376.pin8, SN74HC376.pin9, SN74HC381.pin8, SN74HC381.pin9
  N9: SN74HC376.pin10, SN74HC381.pin10
  N10: SN74HC381.pin1, SN74HC384.pin3
  N11: SN74HC384.pin1, SN74HC384.pin2, R93.Pin_0
  N12: SN74HC384.pin4, SN74HC384.pin5, R96.Pin_0
  N13: R93.Pin_1, R94.Pin_1, R95.Pin_1, R96.Pin_1

notes:
  R0_e
  R1_e
  R0_s
  R1_s
