# Fritzing sketch jcscpu-hmc_clock (saved by Fritzing 0.9.4)
breadboards: 14

parts:
  Part1 = Arduino Nano (Rev3.0) (ICSP)
  Part2 = Arduino Nano (Rev3.0) (ICSP)
  Part3 = Arduino Nano (Rev3.0) (ICSP)
  S1 = Pushbutton [package="[SMD]"]
  R44 = Resistor [tolerance=±5% resistance=1k package=THT]
  R45 = Resistor [tolerance=±5% resistance=1k package=THT]
  R47 = Resistor [tolerance=±5% resistance=1k package=THT]
  R48 = Resistor [tolerance=±5% resistance=1k package=THT]
  R49 = Resistor [tolerance=±5% resistance=1k package=THT]
  R50 = Resistor [tolerance=±5% resistance=1k package=THT]
  R51 = Resistor [tolerance=±5% resistance=1k package=THT]
  R52 = Resistor [tolerance=±5% resistance=1k package=THT]
  R53 = Resistor [tolerance=±5% resistance=10k package="0402 [SMD]"]
  R54 = Resistor [tolerance=±5% resistance=1k package=THT]
  LED60 = LED - 3mm [color="Red (633nm)" package="3 mm [THT]"]
  LED69 = LED - 3mm [color="Red (633nm)" package="3 mm [THT]"]
  LED70 = LED - 3mm [color="Red (633nm)" package="3 mm [THT]"]
  LED112 = LED - 3mm [color="Red (633nm)" package="3 mm [THT]"]
  LED113 = LED - 3mm [color="Red (633nm)" package="3 mm [THT]"]
  LED114 = LED - 3mm [color="Red (633nm)" package="3 mm [THT]"]
  LED115 = LED - 3mm [color="Red (633nm)" package="3 mm [THT]"]
  LED116 = LED - 3mm [color="Red (633nm)" package="3 mm [THT]"]
  LED117 = LED - 3mm [color="Red (633nm)" package="3 mm [THT]"]
  R55 = Resistor [tolerance=±5% resistance=10k package="0402 [SMD]"]
  R56 = Resistor [tolerance=±5% resistance=10k package="0402 [SMD]"]
  R57 = Resistor [tolerance=±5% resistance=10k package="0402 [SMD]"]
  R58 = Resistor [tolerance=±5% resistance=10k package="0402 [SMD]"]

nets:
  N1: Part1.A5, Part2.A5, Part3.A5
  N2: Part1.A4, Part2.A4, Part3.A4
  N3: Part3.D3, LED60.anode
  N4: Part3.D4, S1.Pin_3, S1.Pin_4, R53.Pin_1
  N5: Part3.D5, LED70.anode
  N6: Part3.D6, LED117.anode
  N7: Part3.D7, LED115.anode
  N8: Part3.D8, LED116.anode
  N9: Part3.D9, LED113.anode
  N10: Part3.D10, LED114.anode
  N11: Part3.D11/MOSI, LED112.anode
  N12: Part3.D12/MISO, LED69.anode
  N13: Part3.A3, R57.Pin_0
  N14: Part3.A2, R58.Pin_0
  N15: Part3.A1, R56.Pin_0
  N16: Part3.A0, R55.Pin_0
  N17: S1.Pin_1, S1.Pin_2
  N18: R44.Pin_0, R45.Pin_0, R47.Pin_0, R48.Pin_0, R49.Pin_0, R50.Pin_0, R51.Pin_0, R52.Pin_0, R53.Pin_0, R54.Pin_0
  N19: R44.Pin_1, LED70.cathode
  N20: R45.Pin_1, LED117.cathode
  N21: R47.Pin_1, LED116.cathode
  N22: R48.Pin_1, LED113.cathode
  N23: R49.Pin_1, LED115.cathode
  N24: R50.Pin_1, LED114.cathode
  N25: R51.Pin_1, LED112.cathode
  N26: R52.Pin_1, LED60.cathode
  N27: R54.Pin_1, LED69.cathode
  N28: R55.Pin_1, R56.Pin_1, R57.Pin_1, R58.Pin_1

notes:
  R1_s
  CLK_e  CLK_s           S1       S2       S3       S4       S5       S6                WAIT
