# Fritzing sketch jcscpu-hmc_r2r3 (saved by Fritzing 0.9.4)
breadboards: 14

parts:
  Part1 = Arduino Nano (Rev3.0) (ICSP)
  Part2 = Arduino Nano (Rev3.0) (ICSP)
  Part3 = Arduino Nano (Rev3.0) (ICSP)
  Part4 = Arduino Nano (Rev3.0) (ICSP)  # not connected
  SN74HC377 = IC, DIP package, 20 pins [chip_label=SN74HC373]
  SN74HC379 = IC, DIP package, 20 pins [chip_label=SN74HC373]
  SN74HC383 = IC, DIP package, 14 pins [chip_label=SN74HC00]
  R1 = Resistor [tolerance=±5% resistance=10k package=THT]
  R2 = Resistor [tolerance=±5% resistance=10k package=THT]
  R3 = Resistor [tolerance=±5% resistance=10k package=THT]
  R4 = Resistor [tolerance=±5% resistance=10k package=THT]

nets:
  N1: Part1.A5, Part2.A5, Part3.A5
  N2: Part1.A4, Part2.A4, Part3.A4
  N3: SN74HC377.pin1, SN74HC383.pin6
  N4: SN74HC377.pin2, SN74HC377.pin3, SN74HC379.pin2, SN74HC379.pin3
  N5: SN74HC377.pin4, SN74HC377.pin5, SN74HC379.pin4, SN74HC379.pin5
  N6: SN74HC377.pin7, SN74HC379.pin7
  N7: SN74HC377.pin8, SN74HC377.pin9, SN74HC379.pin8, SN74HC379.pin9
  N8: SN74HC377.pin10, SN74HC379.pin10
  N9: SN74HC377.pin11, R2.Pin_0
  N10: SN74HC377.pin12, SN74HC377.pin13, SN74HC379.pin12, SN74HC379.pin13
  N11: SN74HC377.pin14, SN74HC377.pin15, SN74HC379.pin14, SN74HC379.pin15
  N12: SN74HC377.pin16, SN74HC377.pin17, SN74HC379.pin16, SN74HC379.pin17
  N13: SN74HC377.pin18, SN74HC377.pin19, SN74HC379.pin18, SN74HC379.pin19
  N14: SN74HC377.pin20, SN74HC379.pin20
  N15: SN74HC379.pin1, SN74HC383.pin3
  N16: SN74HC383.pin1, SN74HC383.pin2, R1.Pin_0
  N17: SN74HC383.pin4, SN74HC383.pin5, R4.Pin_0
  N18: R1.Pin_1, R2.Pin_1, R3.Pin_1, R4.Pin_1

notes:
  IR_s
  R1_s
  R2_e
  R3_e
  R3_s
  R2_s
