# Fritzing sketch jcscpu-hmc_ir_iar (saved by Fritzing 0.9.4)
breadboards: 14

parts:
  Part1 = Arduino Nano (Rev3.0) (ICSP)
  Part2 = Arduino Nano (Rev3.0) (ICSP)
  Part3 = Arduino Nano (Rev3.0) (ICSP)
  Part4 = Arduino Nano (Rev3.0) (ICSP)
  SN74HC373 = IC, DIP package, 20 pins [chip_label=SN74HC373]
  SN74HC378 = IC, DIP package, 20 pins [chip_label=SN74HC373]
  SN74HC00 = IC, DIP package, 14 pins [chip_label=SN74HC00]
  R82 = Resistor [tolerance=±5% resistance=1k package=THT]
  R83 = Resistor [tolerance=±5% resistance=1k package=THT]
  R84 = Resistor [tolerance=±5% resistance=1k package=THT]
  R85 = Resistor [tolerance=±5% resistance=1k package=THT]
  R86 = Resistor [tolerance=±5% resistance=1k package=THT]
  R87 = Resistor [tolerance=±5% resistance=1k package=THT]
  R88 = Resistor [tolerance=±5% resistance=1k package=THT]
  R89 = Resistor [tolerance=±5% resistance=1k package=THT]
  LED61 = LED - 3mm [color="Yellow (595nm)" package="3 mm [THT]"]
  LED62 = LED - 3mm [color="Yellow (595nm)" package="3 mm [THT]"]
  LED63 = LED - 3mm [color="Yellow (595nm)" package="3 mm [THT]"]
  LED64 = LED - 3mm [color="Yellow (595nm)" package="3 mm [THT]"]
  LED65 = LED - 3mm [color="Yellow (595nm)" package="3 mm [THT]"]
  LED66 = LED - 3mm [color="Yellow (595nm)" package="3 mm [THT]"]
  LED67 = LED - 3mm [color="Yellow (595nm)" package="3 mm [THT]"]
  LED68 = LED - 3mm [color="Yellow (595nm)" package="3 mm [THT]"]
  R90 = Resistor [tolerance=±5% resistance=10k package=THT]
  R91 = Resistor [tolerance=±5% resistance=10k package=THT]
  R92 = Resistor [tolerance=±5% resistance=10k package=THT]
  R94 = Resistor [tolerance=±5% resistance=10k package=THT]
  R95 = Resistor [tolerance=±5% resistance=10k package=THT]

nets:
  N1: Part1.A5, Part2.A5, Part3.A5, Part4.A5
  N2: Part1.A4, Part2.A4, Part3.A4, Part4.A4
  N3: Part4.D2, R92.Pin_0
  N4: Part4.D3, R90.Pin_1
  N5: Part4.D5, SN74HC378.pin2, LED68.anode
  N6: Part4.D6, SN74HC378.pin5, LED67.anode
  N7: Part4.D7, SN74HC378.pin6, LED66.anode
  N8: Part4.D8, SN74HC378.pin9, LED65.anode
  N9: Part4.D9, LED63.anode
  N10: Part4.D10, LED64.anode
  N11: Part4.D11/MOSI, LED62.anode
  N12: Part4.D12/MISO, LED61.anode
  N13: Part4.A3, R95.Pin_0
  N14: SN74HC373.pin1, SN74HC00.pin6
  N15: SN74HC373.pin2, SN74HC373.pin3
  N16: SN74HC373.pin4, SN74HC373.pin5
  N17: SN74HC373.pin6, SN74HC373.pin7
  N18: SN74HC373.pin8, SN74HC373.pin9
  N19: SN74HC378.pin1, SN74HC378.pin10, R82.Pin_0, R83.Pin_0, R84.Pin_0, R85.Pin_0, R86.Pin_0, R87.Pin_0, R88.Pin_0, R89.Pin_0
  N20: SN74HC00.pin4, SN74HC00.pin5, R91.Pin_0
  N21: R82.Pin_1, LED61.cathode
  N22: R83.Pin_1, LED62.cathode
  N23: R84.Pin_1, LED63.cathode
  N24: R85.Pin_1, LED65.cathode
  N25: R86.Pin_1, LED68.cathode
  N26: R87.Pin_1, LED67.cathode
  N27: R88.Pin_1, LED64.cathode
  N28: R89.Pin_1, LED66.cathode
  N29: R92.Pin_1, R94.Pin_1

notes:
  IAR_e
  IAR_s
  IR_s
  R1_s
