# Fritzing sketch jcscpu-hmc_cs (saved by Fritzing 0.9.4)
breadboards: 14

parts:
  Part1 = Arduino Nano (Rev3.0) (ICSP)
  Part2 = Arduino Nano (Rev3.0) (ICSP)
  Part3 = Arduino Nano (Rev3.0) (ICSP)
  Part4 = Arduino Nano (Rev3.0) (ICSP)
  U28 = 74HC595 [package="DIP16 [THT]"]
  U30 = 74HC595 [package="DIP16 [THT]"]
  U31 = 74HC595 [package="DIP16 [THT]"]
  R55 = Resistor [tolerance=±5% resistance=1k package=THT]
  R56 = Resistor [tolerance=±5% resistance=1k package=THT]
  R57 = Resistor [tolerance=±5% resistance=1k package=THT]
  R58 = Resistor [tolerance=±5% resistance=1k package=THT]
  R59 = Resistor [tolerance=±5% resistance=1k package=THT]
  R60 = Resistor [tolerance=±5% resistance=1k package=THT]
  R61 = Resistor [tolerance=±5% resistance=1k package=THT]
  R62 = Resistor [tolerance=±5% resistance=1k package=THT]
  R63 = Resistor [tolerance=±5% resistance=1k package=THT]
  R64 = Resistor [tolerance=±5% resistance=1k package=THT]
  R65 = Resistor [tolerance=±5% resistance=1k package=THT]
  R66 = Resistor [tolerance=±5% resistance=1k package=THT]
  R67 = Resistor [tolerance=±5% resistance=1k package=THT]
  R68 = Resistor [tolerance=±5% resistance=1k package=THT]
  R69 = Resistor [tolerance=±5% resistance=1k package=THT]
  R70 = Resistor [tolerance=±5% resistance=1k package=THT]
  R71 = Resistor [tolerance=±5% resistance=1k package=THT]
  R72 = Resistor [tolerance=±5% resistance=1k package=THT]
  R73 = Resistor [tolerance=±5% resistance=1k package=THT]
  R74 = Resistor [tolerance=±5% resistance=1k package=THT]
  R75 = Resistor [tolerance=±5% resistance=1k package=THT]
  R76 = Resistor [tolerance=±5% resistance=1k package=THT]
  R77 = Resistor [tolerance=±5% resistance=1k package=THT]
  R78 = Resistor [tolerance=±5% resistance=1k package=THT]
  R79 = Resistor [tolerance=±5% resistance=1k package=THT]
  R90 = Resistor [tolerance=±5% resistance=1k package=THT]
  R91 = Resistor [tolerance=±5% resistance=1k package=THT]
  R92 = Resistor [tolerance=±5% resistance=1k package=THT]
  LED71 = LED - 3mm [color="Yellow (595nm)" package="3 mm [THT]"]
  LED72 = LED - 3mm [color="Yellow (595nm)" package="3 mm [THT]"]
  LED73 = LED - 3mm [color="Yellow (595nm)" package="3 mm [THT]"]
  LED74 = LED - 3mm [color="Yellow (595nm)" package="3 mm [THT]"]
  LED75 = LED - 3mm [color="Yellow (595nm)" package="3 mm [THT]"]
  LED76 = LED - 3mm [color="Yellow (595nm)" package="3 mm [THT]"]
  LED77 = LED - 3mm [color="Yellow (595nm)" package="3 mm [THT]"]
  R93 = Resistor [tolerance=±5% resistance=1k package=THT]
  LED78 = LED - 3mm [color="Yellow (595nm)" package="3 mm [THT]"]
  LED79 = LED - 3mm [color="Yellow (595nm)" package="3 mm [THT]"]
  LED80 = LED - 3mm [color="Yellow (595nm)" package="3 mm [THT]"]
  LED81 = LED - 3mm [color="Yellow (595nm)" package="3 mm [THT]"]
  LED82 = LED - 3mm [color="White (4500K)" package="3 mm [THT]"]
  LED83 = LED - 3mm [color="White (4500K)" package="3 mm [THT]"]
  LED84 = LED - 3mm [color="White (4500K)" package="3 mm [THT]"]
  LED85 = LED - 3mm [color="White (4500K)" package="3 mm [THT]"]
  LED86 = LED - 3mm [color="Yellow (595nm)" package="3 mm [THT]"]
  LED87 = LED - 3mm [color="Blue (505nm)" package="3 mm [THT]"]
  LED88 = LED - 3mm [color="Blue (505nm)" package="3 mm [THT]"]
  LED89 = LED - 3mm [color="Blue (505nm)" package="3 mm [THT]"]
  LED90 = LED - 3mm [color="Blue (505nm)" package="3 mm [THT]"]
  LED91 = LED - 3mm [color="Blue (505nm)" package="3 mm [THT]"]
  LED92 = LED - 3mm [color="Blue (505nm)" package="3 mm [THT]"]
  LED97 = LED - 3mm [color="Blue (505nm)" package="3 mm [THT]"]
  LED98 = LED - 3mm [color="Blue (505nm)" package="3 mm [THT]"]
  LED99 = LED - 3mm [color="Blue (505nm)" package="3 mm [THT]"]
  LED100 = LED - 3mm [color="Green (555nm)" package="3 mm [THT]"]
  LED101 = LED - 3mm [color="Green (555nm)" package="3 mm [THT]"]
  LED102 = LED - 3mm [color="Green (555nm)" package="3 mm [THT]"]
  LED103 = LED - 3mm [color="Red (633nm)" package="3 mm [THT]"]
  U29 = 74HC595 [package="DIP16 [THT]"]

nets:
  N1: Part1.A5, Part2.A5, Part3.A5, Part4.A5
  N2: Part1.A4, Part2.A4, Part3.A4, Part4.A4
  N3: Part1.A2, U28.SH_CP, U30.SH_CP, U31.SH_CP, U29.SH_CP
  N4: Part1.A1, U28.ST_CP, U30.ST_CP, U31.ST_CP, U29.ST_CP
  N5: Part1.A0, U29.DS
  N6: U28.Q1, LED90.anode
  N7: U28.Q2, LED91.anode
  N8: U28.Q3, LED89.anode
  N9: U28.Q5, LED88.anode
  N10: U28.Q6, LED86.anode
  GND: U28.GND, R55.Pin_1, R56.Pin_1, R57.Pin_1, R58.Pin_1, R59.Pin_1, R60.Pin_1, R61.Pin_1, R62.Pin_1, R63.Pin_1, R64.Pin_1, R65.Pin_1, R66.Pin_1, R67.Pin_1, R90.Pin_1, U29.GND
  N11: U28.Q7', U30.DS
  N12: U28.MR, U28.VCC, U29.MR
  N13: U28.OE, U29.OE
  N14: U28.DS, U29.Q7'
  N15: U28.Q0, LED92.anode
  N16: U30.Q1, LED83.anode
  N17: U30.Q2, LED84.anode
  N18: U30.Q3, LED82.anode
  N19: U30.Q4, LED81.anode
  N20: U30.Q5, LED79.anode
  N21: U30.Q6, LED80.anode
  N22: U30.Q7, LED78.anode
  GND_2: U30.GND, U31.GND, R68.Pin_1, R69.Pin_1, R70.Pin_1, R71.Pin_1, R72.Pin_1, R73.Pin_1, R74.Pin_1, R75.Pin_1, R76.Pin_1, R77.Pin_1, R78.Pin_1, R79.Pin_1, R91.Pin_1, R92.Pin_1, R93.Pin_1
  N23: U30.Q7', U31.DS
  VCC: U30.MR, U30.VCC, U31.MR, U31.VCC
  N24: U30.OE, U31.OE
  N25: U30.Q0, LED85.anode
  N26: U31.Q1, LED77.anode
  N27: U31.Q2, LED75.anode
  N28: U31.Q3, LED76.anode
  N29: U31.Q4, LED74.anode
  N30: U31.Q5, LED73.anode
  N31: U31.Q6, LED72.anode
  N32: U31.Q7, LED71.anode
  N33: R55.Pin_0, LED102.cathode
  N34: R56.Pin_0, LED103.cathode
  N35: R57.Pin_0, LED100.cathode
  N36: R58.Pin_0, LED101.cathode
  N37: R59.Pin_0, LED99.cathode
  N38: R60.Pin_0, LED98.cathode
  N39: R61.Pin_0, LED97.cathode
  N40: R62.Pin_0, LED87.cathode
  N41: R63.Pin_0, LED86.cathode
  N42: R64.Pin_0, LED88.cathode
  N43: R65.Pin_0, LED91.cathode
  N44: R66.Pin_0, LED92.cathode
  N45: R67.Pin_0, LED89.cathode
  N46: R68.Pin_0, LED78.cathode
  N47: R69.Pin_0, LED80.cathode
  N48: R70.Pin_0, LED79.cathode
  N49: R71.Pin_0, LED84.cathode
  N50: R72.Pin_0, LED85.cathode
  N51: R73.Pin_0, LED82.cathode
  N52: R74.Pin_0, LED71.cathode
  N53: R75.Pin_0, LED72.cathode
  N54: R76.Pin_0, LED73.cathode
  N55: R77.Pin_0, LED75.cathode
  N56: R78.Pin_0, LED77.cathode
  N57: R79.Pin_0, LED76.cathode
  N58: R90.Pin_0, LED90.cathode
  N59: R91.Pin_0, LED83.cathode
  N60: R92.Pin_0, LED81.cathode
  N61: LED74.cathode, R93.Pin_0
  N62: LED97.anode, U29.Q6
  N63: LED98.anode, U29.Q7
  N64: LED99.anode, U29.Q5
  N65: LED100.anode, U29.Q2
  N66: LED101.anode, U29.Q3
  N67: LED102.anode, U29.Q1
  N68: LED103.anode, U29.Q0

notes:
  HLT
  MAR_s
  RAM_e
  RAM_s
  ALU2
  ALU1
  ALU0
  IAR_e
  IAR_s
  TMP_s
  ACC_e
  BUS1
  ACC_s
  JCOND
  R0_e
  R1_e
  R0_s
  R1_s
  IR_s
  R2_e
  R3_e
  R3_s
  R2_s
  IO_s
  IO_e
  IO_io
