# Fritzing sketch jcscpu-hmc_flag_lines (saved by Fritzing 0.9.4)
breadboards: 14

parts:
  Part1 = Arduino Nano (Rev3.0) (ICSP)  # not connected
  Part2 = Arduino Nano (Rev3.0) (ICSP)
  Part3 = Arduino Nano (Rev3.0) (ICSP)  # not connected
  Part4 = Arduino Nano (Rev3.0) (ICSP)
  SN74HC374 = IC, DIP package, 20 pins [chip_label=SN74HC373]
  SN74HC00 = IC, DIP package, 14 pins [chip_label=SN74HC00]
  SN74HC380 = IC, DIP package, 14 pins [chip_label=SN74HC00]
  SN74HC04 = IC, DIP package, 14 pins [chip_label=SN74HC08]
  SN74HC32 = IC, DIP package, 14 pins [chip_label=SN74HC32]
  R41 = Resistor [tolerance=±5% resistance=1k package=THT]
  R42 = Resistor [tolerance=±5% resistance=1k package=THT]
  R80 = Resistor [tolerance=±5% resistance=1k package=THT]
  R81 = Resistor [tolerance=±5% resistance=1k package=THT]
  LED93 = LED - 3mm [color="Blue (505nm)" package="3 mm [THT]"]
  LED94 = LED - 3mm [color="Blue (505nm)" package="3 mm [THT]"]
  LED95 = LED - 3mm [color="Blue (505nm)" package="3 mm [THT]"]
  LED96 = LED - 3mm [color="Blue (505nm)" package="3 mm [THT]"]

nets:
  N1: Part2.D8, SN74HC00.pin11
  N2: Part2.D9, SN74HC374.pin8
  N3: Part2.D10, SN74HC374.pin7
  N4: Part2.D11/MOSI, SN74HC374.pin4
  N5: Part2.D12/MISO, SN74HC374.pin3
  N6: Part4.D3, SN74HC32.pin3
  N7: Part4.D5, SN74HC04.pin4
  N8: Part4.D6, SN74HC04.pin1
  N9: Part4.D7, SN74HC04.pin10
  N10: Part4.D8, SN74HC04.pin13
  N11: SN74HC374.pin1, SN74HC374.pin10, R41.Pin_0, R42.Pin_0, R80.Pin_0, R81.Pin_0
  N12: SN74HC374.pin2, SN74HC380.pin1, SN74HC04.pin12, LED95.anode
  N13: SN74HC374.pin5, SN74HC04.pin9, LED93.anode
  N14: SN74HC374.pin6, SN74HC04.pin2, LED94.anode
  N15: SN74HC374.pin9, SN74HC04.pin5, LED96.anode
  N16: SN74HC374.pin20, SN74HC00.pin14, SN74HC380.pin14
  N17: SN74HC00.pin1, SN74HC380.pin6, SN74HC380.pin9
  N18: SN74HC00.pin3, SN74HC00.pin12, SN74HC00.pin13
  N19: SN74HC00.pin7, SN74HC380.pin7
  N20: SN74HC380.pin2, SN74HC380.pin12
  N21: SN74HC380.pin3, SN74HC380.pin13
  N22: SN74HC380.pin4, SN74HC380.pin5, SN74HC380.pin8
  N23: SN74HC380.pin10, SN74HC380.pin11
  N24: SN74HC04.pin3, SN74HC32.pin4
  N25: SN74HC04.pin6, SN74HC32.pin5
  N26: SN74HC04.pin7, SN74HC32.pin7
  N27: SN74HC04.pin8, SN74HC32.pin11
  N28: SN74HC04.pin11, SN74HC32.pin9
  N29: SN74HC04.pin14, SN74HC32.pin14
  N30: SN74HC32.pin1, SN74HC32.pin8
  N31: SN74HC32.pin2, SN74HC32.pin6
  N32: R41.Pin_1, LED93.cathode
  N33: R42.Pin_1, LED96.cathode
  N34: R80.Pin_1, LED94.cathode
  N35: R81.Pin_1, LED95.cathode

notes:
  R1_s
