# Fritzing sketch 1-bit Memory (saved by Fritzing 0.9.4)
breadboards: 1

parts:
  IC1 = IC, DIP package, 14 pins [chip_label=SN74HC00]
  LED1 = LED - 5mm [color="Red (633nm)" package="5 mm [THT]"]
  R1 = Resistor [tolerance=±5% resistance=1k package=THT]
  Part1 = Arduino Nano (Rev3.0)

nets:
  N1: IC1.pin1, IC1.pin2, IC1.pin7, IC1.pin12, R1.Pin_0, Part1.GND
  N2: IC1.pin3, IC1.pin4, IC1.pin13
  N3: IC1.pin5, IC1.pin8
  N4: IC1.pin6, IC1.pin9, LED1.cathode
  N5: IC1.pin10, IC1.pin11
  N6: IC1.pin14, Part1.5V
  N7: LED1.anode, R1.Pin_1
