# Fritzing sketch Register (saved by Fritzing 0.9.4)
breadboards: 3

parts:
  IC3 = IC, DIP package, 14 pins [chip_label=SN74HC00]
  IC4 = IC, DIP package, 14 pins [chip_label=SN74HC00]
  IC5 = IC, DIP package, 14 pins [chip_label=SN74HC00]
  IC6 = IC, DIP package, 14 pins [chip_label=SN74HC00]
  IC7 = IC, DIP package, 14 pins [chip_label=SN74HC00]
  IC8 = IC, DIP package, 14 pins [chip_label=SN74HC00]
  IC9 = IC, DIP package, 14 pins [chip_label=SN74HC00]
  IC10 = IC, DIP package, 14 pins [chip_label=SN74HC00]
  IC11 = IC, DIP package, 14 pins [chip_label=SN74HC00]
  IC12 = IC, DIP package, 14 pins [chip_label=SN74HC00]
  IC13 = IC, DIP package, 14 pins [chip_label=SN74HC00]
  IC14 = IC, DIP package, 14 pins [chip_label=SN74HC00]
  IC15 = IC, DIP package, 14 pins [chip_label=SN74HC00]
  IC16 = IC, DIP package, 14 pins [chip_label=SN74HC00]
  IC17 = IC, DIP package, 14 pins [chip_label=SN74HC00]
  IC18 = IC, DIP package, 14 pins [chip_label=SN74HC00]
  S1 = Pushbutton [package="[THT]"]
  R1 = Resistor [tolerance=±5% resistance=10k package="2512 [SMD]"]
  S2 = Pushbutton [package="[THT]"]
  R2 = Resistor [tolerance=±5% resistance=10k package="2512 [SMD]"]
  LED1 = LED - 5mm [color="Yellow (595nm)" package="5 mm [THT]"]
  R3 = Resistor [tolerance=±5% resistance=1k package=THT]
  R4 = Resistor [tolerance=±5% resistance=1k package=THT]
  R5 = Resistor [tolerance=±5% resistance=1k package=THT]
  R6 = Resistor [tolerance=±5% resistance=1k package=THT]
  R7 = Resistor [tolerance=±5% resistance=1k package=THT]
  R8 = Resistor [tolerance=±5% resistance=1k package=THT]
  R9 = Resistor [tolerance=±5% resistance=1k package=THT]
  R10 = Resistor [tolerance=±5% resistance=1k package=THT]
  LED2 = LED - 5mm [color="Yellow (595nm)" package="5 mm [THT]"]
  LED3 = LED - 5mm [color="Yellow (595nm)" package="5 mm [THT]"]
  LED4 = LED - 5mm [color="Yellow (595nm)" package="5 mm [THT]"]
  LED5 = LED - 5mm [color="Yellow (595nm)" package="5 mm [THT]"]
  LED6 = LED - 5mm [color="Yellow (595nm)" package="5 mm [THT]"]
  LED7 = LED - 5mm [color="Yellow (595nm)" package="5 mm [THT]"]
  LED8 = LED - 5mm [color="Yellow (595nm)" package="5 mm [THT]"]
  SW1 = DIP Switch 8 Position [package=dipswitch-08]
  R12 = Resistor [tolerance=±5% resistance=10k package="2512 [SMD]"]
  R13 = Resistor [tolerance=±5% resistance=10k package="2512 [SMD]"]
  R14 = Resistor [tolerance=±5% resistance=10k package="2512 [SMD]"]
  R15 = Resistor [tolerance=±5% resistance=10k package="2512 [SMD]"]
  R16 = Resistor [tolerance=±5% resistance=10k package="2512 [SMD]"]
  R17 = Resistor [tolerance=±5% resistance=10k package="2512 [SMD]"]
  R18 = Resistor [tolerance=±5% resistance=10k package="2512 [SMD]"]
  R19 = Resistor [tolerance=±5% resistance=10k package="2512 [SMD]"]

nets:
  N1: IC3.pin1, SW1.16, R19.Pin_1
  N2: IC3.pin2, IC3.pin12, IC4.pin2, IC4.pin12, IC5.pin2, IC5.pin12, IC6.pin2, IC6.pin12, IC7.pin2, IC7.pin12, IC8.pin2, IC8.pin12, IC9.pin2, IC9.pin12, IC10.pin2, IC10.pin12, S1.Pin_3, S1.Pin_4, R1.Pin_0
  N3: IC3.pin3, IC3.pin4, IC3.pin13
  N4: IC3.pin5, IC3.pin8, IC11.pin2
  N5: IC3.pin6, IC3.pin9
  N6: IC3.pin7, IC5.pin7, IC6.pin7, IC8.pin7, IC9.pin7, IC10.pin7
  N7: IC3.pin10, IC3.pin11
  N8: IC3.pin14, IC4.pin14, IC5.pin14, IC6.pin14, IC7.pin14, IC8.pin14, IC9.pin14, IC10.pin14
  N9: IC4.pin1, SW1.15, R18.Pin_1
  N10: IC4.pin3, IC4.pin4, IC4.pin13
  N11: IC4.pin5, IC4.pin8, IC12.pin2
  N12: IC4.pin6, IC4.pin9
  N13: IC4.pin7, IC7.pin7, R12.Pin_0, R13.Pin_0, R14.Pin_0, R16.Pin_0, R17.Pin_0, R18.Pin_0, R19.Pin_0
  N14: IC4.pin10, IC4.pin11
  N15: IC5.pin1, SW1.14, R17.Pin_1
  N16: IC5.pin3, IC5.pin4, IC5.pin13
  N17: IC5.pin5, IC5.pin8, IC13.pin2
  N18: IC5.pin6, IC5.pin9
  N19: IC5.pin10, IC5.pin11
  N20: IC6.pin1, SW1.13, R16.Pin_1
  N21: IC6.pin3, IC6.pin4, IC6.pin13
  N22: IC6.pin5, IC6.pin8, IC14.pin2, IC15.pin1, IC16.pin1, IC17.pin1, IC18.pin1
  N23: IC6.pin6, IC6.pin9
  N24: IC6.pin10, IC6.pin11
  N25: IC7.pin1, SW1.12, R15.Pin_1
  N26: IC7.pin3, IC7.pin4, IC7.pin13
  N27: IC7.pin5, IC7.pin8, IC15.pin2
  N28: IC7.pin6, IC7.pin9
  N29: IC7.pin10, IC7.pin11
  N30: IC8.pin1, SW1.11, R14.Pin_1
  N31: IC8.pin3, IC8.pin4, IC8.pin13
  N32: IC8.pin5, IC8.pin8, IC16.pin2
  N33: IC8.pin6, IC8.pin9
  N34: IC8.pin10, IC8.pin11
  N35: IC9.pin1, SW1.10, R13.Pin_1
  N36: IC9.pin3, IC9.pin4, IC9.pin13
  N37: IC9.pin5, IC9.pin8, IC17.pin2
  N38: IC9.pin6, IC9.pin9
  N39: IC9.pin10, IC9.pin11
  N40: IC10.pin1, SW1.9, R12.Pin_1
  N41: IC10.pin3, IC10.pin4, IC10.pin13
  N42: IC10.pin5, IC10.pin8, IC18.pin2
  N43: IC10.pin6, IC10.pin9
  N44: IC10.pin10, IC10.pin11
  N45: IC11.pin1, IC12.pin1, IC13.pin1, IC14.pin1, S2.Pin_3, S2.Pin_4, R2.Pin_0
  N46: IC11.pin3, IC11.pin4, IC11.pin5
  N47: IC11.pin6, LED1.anode
  N48: IC11.pin7, IC12.pin7, IC13.pin7, IC14.pin7, IC15.pin7, IC16.pin7, IC17.pin7
  N49: IC11.pin14, IC12.pin14, IC13.pin14, IC14.pin14, IC15.pin14, IC16.pin14, IC17.pin14, IC18.pin14
  N50: IC12.pin3, IC12.pin4, IC12.pin5
  N51: IC12.pin6, LED3.anode
  N52: IC13.pin3, IC13.pin4, IC13.pin5
  N53: IC13.pin6, LED2.anode
  N54: IC14.pin3, IC14.pin4, IC14.pin5
  N55: IC14.pin6, LED4.anode
  N56: IC15.pin3, IC15.pin4, IC15.pin5
  N57: IC15.pin6, LED8.anode
  N58: IC16.pin3, IC16.pin4, IC16.pin5
  N59: IC16.pin6, LED7.anode
  N60: IC17.pin3, IC17.pin4, IC17.pin5
  N61: IC17.pin6, LED6.anode
  N62: IC18.pin3, IC18.pin4, IC18.pin5
  N63: IC18.pin6, LED5.anode
  N64: S1.Pin_1, S1.Pin_2, S2.Pin_1, S2.Pin_2, SW1.1, SW1.2, SW1.3, SW1.4, SW1.5, SW1.6, SW1.7, SW1.8
  N65: R1.Pin_1, R2.Pin_1, R3.Pin_1, R4.Pin_1, R5.Pin_1, R6.Pin_1, R7.Pin_1, R8.Pin_1, R9.Pin_1, R10.Pin_1
  N66: LED1.cathode, R3.Pin_0
  N67: R4.Pin_0, LED3.cathode
  N68: R5.Pin_0, LED2.cathode
  N69: R6.Pin_0, LED5.cathode
  N70: R7.Pin_0, LED6.cathode
  N71: R8.Pin_0, LED7.cathode
  N72: R9.Pin_0, LED8.cathode
  N73: R10.Pin_0, LED4.cathode
