# Fritzing sketch jcscpu-hmc (saved by Fritzing 0.9.4)
breadboards: 16

parts:
  Part1 = Arduino Nano (Rev3.0) (ICSP)
  Part2 = Arduino Nano (Rev3.0) (ICSP)
  Part3 = Arduino Nano (Rev3.0) (ICSP)
  Part4 = Arduino Nano (Rev3.0) (ICSP)
  SW1 = DIP Switch 8 Position [package=dipswitch-08]
  S1 = Pushbutton [package="[SMD]"]
  U28 = 74HC595 [package="DIP16 [THT]"]
  U30 = 74HC595 [package="DIP16 [THT]"]
  U31 = 74HC595 [package="DIP16 [THT]"]
  R32 = Resistor [tolerance=±5% resistance=10k package="0402 [SMD]"]
  R33 = Resistor [tolerance=±5% resistance=10k package="0402 [SMD]"]
  R34 = Resistor [tolerance=±5% resistance=10k package="0402 [SMD]"]
  R35 = Resistor [tolerance=±5% resistance=10k package="0402 [SMD]"]
  R36 = Resistor [tolerance=±5% resistance=10k package="0402 [SMD]"]
  R37 = Resistor [tolerance=±5% resistance=10k package="0402 [SMD]"]
  R38 = Resistor [tolerance=±5% resistance=10k package="0402 [SMD]"]
  R5 = Resistor [tolerance=±5% resistance=1k package=THT]
  R7 = Resistor [tolerance=±5% resistance=1k package=THT]
  R6 = Resistor [tolerance=±5% resistance=1k package=THT]
  R4 = Resistor [tolerance=±5% resistance=1k package=THT]
  R3 = Resistor [tolerance=±5% resistance=1k package=THT]
  R2 = Resistor [tolerance=±5% resistance=1k package=THT]
  R8 = Resistor [tolerance=±5% resistance=1k package=THT]
  R1 = Resistor [tolerance=±5% resistance=1k package=THT]
  R39 = Resistor [tolerance=±5% resistance=10k package="0402 [SMD]"]
  SN74HC373 = IC, DIP package, 20 pins [chip_label=SN74HC373]
  SN74HC376 = IC, DIP package, 20 pins [chip_label=SN74HC373]
  SN74HC377 = IC, DIP package, 20 pins [chip_label=SN74HC373]
  SN74HC378 = IC, DIP package, 20 pins [chip_label=SN74HC373]
  SN74HC379 = IC, DIP package, 20 pins [chip_label=SN74HC373]
  SN74HC374 = IC, DIP package, 20 pins [chip_label=SN74HC373]
  SN74HC00 = IC, DIP package, 14 pins [chip_label=SN74HC00]
  SN74HC380 = IC, DIP package, 14 pins [chip_label=SN74HC00]
  SN74HC381 = IC, DIP package, 20 pins [chip_label=SN74HC373]
  R44 = Resistor [tolerance=±5% resistance=1k package=THT]
  R45 = Resistor [tolerance=±5% resistance=1k package=THT]
  R47 = Resistor [tolerance=±5% resistance=1k package=THT]
  R48 = Resistor [tolerance=±5% resistance=1k package=THT]
  R49 = Resistor [tolerance=±5% resistance=1k package=THT]
  R50 = Resistor [tolerance=±5% resistance=1k package=THT]
  R51 = Resistor [tolerance=±5% resistance=1k package=THT]
  R52 = Resistor [tolerance=±5% resistance=1k package=THT]
  R53 = Resistor [tolerance=±5% resistance=10k package="0402 [SMD]"]
  SN74HC383 = IC, DIP package, 14 pins [chip_label=SN74HC00]
  SN74HC04 = IC, DIP package, 14 pins [chip_label=SN74HC08]
  SN74HC32 = IC, DIP package, 14 pins [chip_label=SN74HC32]
  R54 = Resistor [tolerance=±5% resistance=1k package=THT]
  SN74HC384 = IC, DIP package, 14 pins [chip_label=SN74HC00]
  R41 = Resistor [tolerance=±5% resistance=1k package=THT]
  R42 = Resistor [tolerance=±5% resistance=1k package=THT]
  R55 = Resistor [tolerance=±5% resistance=1k package=THT]
  R56 = Resistor [tolerance=±5% resistance=1k package=THT]
  R57 = Resistor [tolerance=±5% resistance=1k package=THT]
  R58 = Resistor [tolerance=±5% resistance=1k package=THT]
  R59 = Resistor [tolerance=±5% resistance=1k package=THT]
  R60 = Resistor [tolerance=±5% resistance=1k package=THT]
  R61 = Resistor [tolerance=±5% resistance=1k package=THT]
  R62 = Resistor [tolerance=±5% resistance=1k package=THT]
  R63 = Resistor [tolerance=±5% resistance=1k package=THT]
  R64 = Resistor [tolerance=±5% resistance=1k package=THT]
  R65 = Resistor [tolerance=±5% resistance=1k package=THT]
  R66 = Resistor [tolerance=±5% resistance=1k package=THT]
  R67 = Resistor [tolerance=±5% resistance=1k package=THT]
  R68 = Resistor [tolerance=±5% resistance=1k package=THT]
  R69 = Resistor [tolerance=±5% resistance=1k package=THT]
  R70 = Resistor [tolerance=±5% resistance=1k package=THT]
  R71 = Resistor [tolerance=±5% resistance=1k package=THT]
  R72 = Resistor [tolerance=±5% resistance=1k package=THT]
  R73 = Resistor [tolerance=±5% resistance=1k package=THT]
  R74 = Resistor [tolerance=±5% resistance=1k package=THT]
  R75 = Resistor [tolerance=±5% resistance=1k package=THT]
  R76 = Resistor [tolerance=±5% resistance=1k package=THT]
  R77 = Resistor [tolerance=±5% resistance=1k package=THT]
  R78 = Resistor [tolerance=±5% resistance=1k package=THT]
  R79 = Resistor [tolerance=±5% resistance=1k package=THT]
  R80 = Resistor [tolerance=±5% resistance=1k package=THT]
  R81 = Resistor [tolerance=±5% resistance=1k package=THT]
  LED60 = LED - 3mm [color="Red (633nm)" package="3 mm [THT]"]
  R82 = Resistor [tolerance=±5% resistance=1k package=THT]
  R83 = Resistor [tolerance=±5% resistance=1k package=THT]
  R84 = Resistor [tolerance=±5% resistance=1k package=THT]
  R85 = Resistor [tolerance=±5% resistance=1k package=THT]
  R86 = Resistor [tolerance=±5% resistance=1k package=THT]
  R87 = Resistor [tolerance=±5% resistance=1k package=THT]
  R88 = Resistor [tolerance=±5% resistance=1k package=THT]
  R89 = Resistor [tolerance=±5% resistance=1k package=THT]
  LED61 = LED - 3mm [color="Yellow (595nm)" package="3 mm [THT]"]
  LED62 = LED - 3mm [color="Yellow (595nm)" package="3 mm [THT]"]
  LED63 = LED - 3mm [color="Yellow (595nm)" package="3 mm [THT]"]
  LED64 = LED - 3mm [color="Yellow (595nm)" package="3 mm [THT]"]
  LED65 = LED - 3mm [color="Yellow (595nm)" package="3 mm [THT]"]
  LED66 = LED - 3mm [color="Yellow (595nm)" package="3 mm [THT]"]
  LED67 = LED - 3mm [color="Yellow (595nm)" package="3 mm [THT]"]
  LED68 = LED - 3mm [color="Yellow (595nm)" package="3 mm [THT]"]
  LED69 = LED - 3mm [color="Red (633nm)" package="3 mm [THT]"]
  LED70 = LED - 3mm [color="Red (633nm)" package="3 mm [THT]"]
  R90 = Resistor [tolerance=±5% resistance=1k package=THT]
  R91 = Resistor [tolerance=±5% resistance=1k package=THT]
  R92 = Resistor [tolerance=±5% resistance=1k package=THT]
  LED71 = LED - 3mm [color="Yellow (595nm)" package="3 mm [THT]"]
  LED72 = LED - 3mm [color="Yellow (595nm)" package="3 mm [THT]"]
  LED73 = LED - 3mm [color="Yellow (595nm)" package="3 mm [THT]"]
  LED74 = LED - 3mm [color="Yellow (595nm)" package="3 mm [THT]"]
  LED75 = LED - 3mm [color="Yellow (595nm)" package="3 mm [THT]"]
  LED76 = LED - 3mm [color="Yellow (595nm)" package="3 mm [THT]"]
  LED77 = LED - 3mm [color="Yellow (595nm)" package="3 mm [THT]"]
  R93 = Resistor [tolerance=±5% resistance=1k package=THT]
  LED78 = LED - 3mm [color="Yellow (595nm)" package="3 mm [THT]"]
  LED79 = LED - 3mm [color="Yellow (595nm)" package="3 mm [THT]"]
  LED80 = LED - 3mm [color="Yellow (595nm)" package="3 mm [THT]"]
  LED81 = LED - 3mm [color="Yellow (595nm)" package="3 mm [THT]"]
  LED82 = LED - 3mm [color="White (4500K)" package="3 mm [THT]"]
  LED83 = LED - 3mm [color="White (4500K)" package="3 mm [THT]"]
  LED84 = LED - 3mm [color="White (4500K)" package="3 mm [THT]"]
  LED85 = LED - 3mm [color="White (4500K)" package="3 mm [THT]"]
  LED86 = LED - 3mm [color="Yellow (595nm)" package="3 mm [THT]"]
  LED87 = LED - 3mm [color="Blue (505nm)" package="3 mm [THT]"]
  LED88 = LED - 3mm [color="Blue (505nm)" package="3 mm [THT]"]
  LED89 = LED - 3mm [color="Blue (505nm)" package="3 mm [THT]"]
  LED90 = LED - 3mm [color="Blue (505nm)" package="3 mm [THT]"]
  LED91 = LED - 3mm [color="Blue (505nm)" package="3 mm [THT]"]
  LED92 = LED - 3mm [color="Blue (505nm)" package="3 mm [THT]"]
  LED93 = LED - 3mm [color="Blue (505nm)" package="3 mm [THT]"]
  LED94 = LED - 3mm [color="Blue (505nm)" package="3 mm [THT]"]
  LED95 = LED - 3mm [color="Blue (505nm)" package="3 mm [THT]"]
  LED96 = LED - 3mm [color="Blue (505nm)" package="3 mm [THT]"]
  LED97 = LED - 3mm [color="Blue (505nm)" package="3 mm [THT]"]
  LED98 = LED - 3mm [color="Blue (505nm)" package="3 mm [THT]"]
  LED99 = LED - 3mm [color="Blue (505nm)" package="3 mm [THT]"]
  LED100 = LED - 3mm [color="Green (555nm)" package="3 mm [THT]"]
  LED101 = LED - 3mm [color="Green (555nm)" package="3 mm [THT]"]
  LED102 = LED - 3mm [color="Green (555nm)" package="3 mm [THT]"]
  LED103 = LED - 3mm [color="Red (633nm)" package="3 mm [THT]"]
  LED104 = LED - 3mm [color="Green (555nm)" package="3 mm [THT]"]
  LED105 = LED - 3mm [color="Green (555nm)" package="3 mm [THT]"]
  LED106 = LED - 3mm [color="Green (555nm)" package="3 mm [THT]"]
  LED107 = LED - 3mm [color="Green (555nm)" package="3 mm [THT]"]
  LED108 = LED - 3mm [color="Green (555nm)" package="3 mm [THT]"]
  LED109 = LED - 3mm [color="Green (555nm)" package="3 mm [THT]"]
  LED110 = LED - 3mm [color="Green (555nm)" package="3 mm [THT]"]
  LED111 = LED - 3mm [color="Green (555nm)" package="3 mm [THT]"]
  LED112 = LED - 3mm [color="Red (633nm)" package="3 mm [THT]"]
  LED113 = LED - 3mm [color="Red (633nm)" package="3 mm [THT]"]
  LED114 = LED - 3mm [color="Red (633nm)" package="3 mm [THT]"]
  LED115 = LED - 3mm [color="Red (633nm)" package="3 mm [THT]"]
  LED116 = LED - 3mm [color="Red (633nm)" package="3 mm [THT]"]
  LED117 = LED - 3mm [color="Red (633nm)" package="3 mm [THT]"]
  U29 = 74HC595 [package="DIP16 [THT]"]

nets:
  GND: Part1.GND, Part2.GND, Part3.GND, Part4.GND, U28.GND, U28.OE, U30.GND, U30.OE, U31.GND, U31.OE, R5.Pin_0, R7.Pin_0, R6.Pin_0, R4.Pin_0, R3.Pin_0, R2.Pin_0, R8.Pin_0, R1.Pin_0, SN74HC373.pin10, SN74HC374.pin1, SN74HC374.pin10, SN74HC00.pin7, SN74HC380.pin7, SN74HC383.pin7, SN74HC04.pin7, SN74HC32.pin7, SN74HC384.pin7, R41.Pin_0, R42.Pin_0, R55.Pin_1, R56.Pin_1, R57.Pin_1, R58.Pin_1, R59.Pin_1, R60.Pin_1, R61.Pin_1, R62.Pin_1, R63.Pin_1, R64.Pin_1, R65.Pin_1, R66.Pin_1, R67.Pin_1, R68.Pin_1, R69.Pin_1, R70.Pin_1, R71.Pin_1, R72.Pin_1, R73.Pin_1, R74.Pin_1, R75.Pin_1, R76.Pin_1, R77.Pin_1, R78.Pin_1, R79.Pin_1, R80.Pin_0, R81.Pin_0, R90.Pin_1, R91.Pin_1, R92.Pin_1, R93.Pin_1, U29.GND, U29.OE
  N1: Part1.D2, LED101.anode, U29.Q3
  N2: Part1.D3, LED100.anode, U29.Q2
  N3: Part1.D4, LED102.anode, U29.Q1
  N4: Part1.D5, SW1.9, R38.Pin_0, SN74HC373.pin2, SN74HC373.pin3, SN74HC376.pin2, SN74HC376.pin3, SN74HC377.pin2, SN74HC377.pin3, SN74HC378.pin3, SN74HC379.pin2, SN74HC379.pin3, SN74HC381.pin2, SN74HC381.pin3, LED111.anode
  N5: Part1.D6, SW1.10, R37.Pin_0, SN74HC373.pin4, SN74HC373.pin5, SN74HC376.pin4, SN74HC376.pin5, SN74HC377.pin4, SN74HC377.pin5, SN74HC378.pin4, SN74HC379.pin4, SN74HC379.pin5, SN74HC381.pin4, SN74HC381.pin5, LED110.anode
  N6: Part1.D7, SW1.11, R39.Pin_0, SN74HC373.pin6, SN74HC373.pin7, SN74HC376.pin6, SN74HC376.pin7, SN74HC377.pin7, SN74HC378.pin7, SN74HC379.pin7, SN74HC381.pin6, SN74HC381.pin7, LED108.anode
  N7: Part1.D8, SW1.12, R36.Pin_0, SN74HC373.pin8, SN74HC373.pin9, SN74HC376.pin8, SN74HC376.pin9, SN74HC377.pin8, SN74HC377.pin9, SN74HC378.pin8, SN74HC379.pin8, SN74HC379.pin9, SN74HC381.pin8, SN74HC381.pin9, LED107.anode
  N8: Part1.D9, SW1.13, R34.Pin_0, SN74HC377.pin12, SN74HC377.pin13, SN74HC379.pin12, SN74HC379.pin13, LED109.anode
  N9: Part1.D10, SW1.14, R35.Pin_0, SN74HC377.pin14, SN74HC377.pin15, SN74HC379.pin14, SN74HC379.pin15, LED105.anode
  N10: Part1.D11/MOSI, SW1.15, R33.Pin_0, SN74HC377.pin16, SN74HC377.pin17, SN74HC379.pin16, SN74HC379.pin17, LED104.anode
  N11: Part1.D12/MISO, SW1.16, R32.Pin_0, SN74HC377.pin18, SN74HC377.pin19, SN74HC379.pin18, SN74HC379.pin19, LED106.anode
  5V: Part1.5V, Part2.5V, Part3.5V, Part4.5V, SW1.1, SW1.2, SW1.3, SW1.4, SW1.5, SW1.6, SW1.7, SW1.8, S1.Pin_1, S1.Pin_2, U28.MR, U28.VCC, U30.MR, U30.VCC, U31.MR, U31.VCC, SN74HC377.pin20, SN74HC379.pin20, SN74HC374.pin20, SN74HC00.pin14, SN74HC380.pin14, SN74HC383.pin14, SN74HC04.pin14, SN74HC32.pin14, SN74HC384.pin14, U29.MR, U29.VCC
  N12: Part1.A5, Part2.A5, Part3.A5, Part4.A5
  N13: Part1.A4, Part2.A4, Part3.A4, Part4.A4
  N14: Part1.A3, LED103.anode
  N15: Part1.A2, U28.SH_CP, U30.SH_CP, U31.SH_CP, U29.SH_CP
  N16: Part1.A1, U28.ST_CP, U30.ST_CP, U31.ST_CP, U29.ST_CP
  N17: Part1.A0, U29.DS
  N18: Part2.D2, U28.Q3, LED89.anode
  N19: Part2.D5, U28.Q2, LED91.anode
  N20: Part2.D6, U28.Q1, LED90.anode
  N21: Part2.D7, U28.Q0, SN74HC380.pin2, SN74HC380.pin12, LED92.anode
  N22: Part2.D8, SN74HC00.pin11
  N23: Part2.D9, SN74HC374.pin8
  N24: Part2.D10, SN74HC374.pin7
  N25: Part2.D11/MOSI, SN74HC374.pin4
  N26: Part2.D12/MISO, SN74HC374.pin3
  N27: Part2.A2, LED98.anode, U29.Q7
  N28: Part2.A1, LED97.anode, U29.Q6
  N29: Part2.A0, LED99.anode, U29.Q5
  N30: Part3.D3, LED60.anode
  N31: Part3.D4, S1.Pin_3, S1.Pin_4, R53.Pin_1
  N32: Part3.D5, LED70.anode
  N33: Part3.D6, LED117.anode
  N34: Part3.D7, LED115.anode
  N35: Part3.D8, LED116.anode
  N36: Part3.D9, LED113.anode
  N37: Part3.D10, LED114.anode
  N38: Part3.D11/MOSI, LED112.anode
  N39: Part3.D12/MISO, LED69.anode
  N40: Part3.A3, U30.Q3, LED82.anode
  N41: Part3.A2, U30.Q2, LED84.anode
  N42: Part3.A1, U30.Q1, LED83.anode
  N43: Part3.A0, U30.Q0, LED85.anode
  N44: Part4.D2, U31.Q2, LED75.anode
  N45: Part4.D3, SN74HC32.pin3
  N46: Part4.D5, SN74HC378.pin2, SN74HC04.pin4, LED68.anode
  N47: Part4.D6, SN74HC378.pin5, SN74HC04.pin1, LED67.anode
  N48: Part4.D7, SN74HC378.pin6, SN74HC04.pin10, LED66.anode
  N49: Part4.D8, SN74HC378.pin9, SN74HC04.pin13, LED65.anode
  N50: Part4.D9, LED63.anode
  N51: Part4.D10, LED64.anode
  N52: Part4.D11/MOSI, LED62.anode
  N53: Part4.D12/MISO, LED61.anode
  N54: Part4.A3, U31.Q1, LED77.anode
  N55: U28.Q5, SN74HC00.pin2, LED88.anode
  N56: U28.Q6, SN74HC00.pin4, SN74HC00.pin5, LED86.anode
  N57: U28.Q7', U30.DS
  N58: U28.DS, U29.Q7'
  N59: U30.Q4, SN74HC384.pin1, SN74HC384.pin2, LED81.anode
  N60: U30.Q5, SN74HC384.pin4, SN74HC384.pin5, LED79.anode
  N61: U30.Q6, LED80.anode
  N62: U30.Q7, LED78.anode
  N63: U30.Q7', U31.DS
  N64: U31.Q3, SN74HC383.pin1, SN74HC383.pin2, LED76.anode
  N65: U31.Q4, SN74HC383.pin4, SN74HC383.pin5, LED74.anode
  N66: U31.Q5, SN74HC377.pin11, LED73.anode
  N67: U31.Q6, LED72.anode
  N68: U31.Q7, LED71.anode
  N69: R7.Pin_1, LED110.cathode
  N70: R6.Pin_1, LED111.cathode
  N71: R4.Pin_1, LED107.cathode
  N72: R3.Pin_1, LED109.cathode
  N73: R2.Pin_1, LED105.cathode
  N74: R8.Pin_1, LED104.cathode
  N75: R1.Pin_1, LED106.cathode
  N76: SN74HC373.pin1, SN74HC00.pin6
  N77: SN74HC376.pin1, SN74HC384.pin6
  N78: SN74HC376.pin10, SN74HC377.pin10, SN74HC378.pin1, SN74HC378.pin10, SN74HC379.pin10, SN74HC381.pin10, R44.Pin_0, R45.Pin_0, R47.Pin_0, R48.Pin_0, R49.Pin_0, R50.Pin_0, R51.Pin_0, R52.Pin_0, R53.Pin_0, R54.Pin_0, R82.Pin_0, R83.Pin_0, R84.Pin_0, R85.Pin_0, R86.Pin_0, R87.Pin_0, R88.Pin_0, R89.Pin_0
  N79: SN74HC377.pin1, SN74HC383.pin6
  N80: SN74HC379.pin1, SN74HC383.pin3
  N81: SN74HC374.pin2, SN74HC380.pin1, SN74HC04.pin12, LED95.anode
  N82: SN74HC374.pin5, SN74HC04.pin9, LED93.anode
  N83: SN74HC374.pin6, SN74HC04.pin2, LED94.anode
  N84: SN74HC374.pin9, SN74HC04.pin5, LED96.anode
  N85: SN74HC374.pin11, LED87.anode
  N86: SN74HC00.pin1, SN74HC380.pin6, SN74HC380.pin9
  N87: SN74HC00.pin3, SN74HC00.pin12, SN74HC00.pin13
  N88: SN74HC380.pin3, SN74HC380.pin13
  N89: SN74HC380.pin4, SN74HC380.pin5, SN74HC380.pin8
  N90: SN74HC380.pin10, SN74HC380.pin11
  N91: SN74HC381.pin1, SN74HC384.pin3
  N92: R44.Pin_1, LED70.cathode
  N93: R45.Pin_1, LED117.cathode
  N94: R47.Pin_1, LED116.cathode
  N95: R48.Pin_1, LED113.cathode
  N96: R49.Pin_1, LED115.cathode
  N97: R50.Pin_1, LED114.cathode
  N98: R51.Pin_1, LED112.cathode
  N99: R52.Pin_1, LED60.cathode
  N100: SN74HC04.pin3, SN74HC32.pin4
  N101: SN74HC04.pin6, SN74HC32.pin5
  N102: SN74HC04.pin8, SN74HC32.pin11
  N103: SN74HC04.pin11, SN74HC32.pin9
  N104: SN74HC32.pin1, SN74HC32.pin8
  N105: SN74HC32.pin2, SN74HC32.pin6
  N106: R54.Pin_1, LED69.cathode
  N107: R41.Pin_1, LED93.cathode
  N108: R42.Pin_1, LED96.cathode
  N109: R55.Pin_0, LED102.cathode
  N110: R56.Pin_0, LED103.cathode
  N111: R57.Pin_0, LED100.cathode
  N112: R58.Pin_0, LED101.cathode
  N113: R59.Pin_0, LED99.cathode
  N114: R60.Pin_0, LED98.cathode
  N115: R61.Pin_0, LED97.cathode
  N116: R62.Pin_0, LED87.cathode
  N117: R63.Pin_0, LED86.cathode
  N118: R64.Pin_0, LED88.cathode
  N119: R65.Pin_0, LED91.cathode
  N120: R66.Pin_0, LED92.cathode
  N121: R67.Pin_0, LED89.cathode
  N122: R68.Pin_0, LED78.cathode
  N123: R69.Pin_0, LED80.cathode
  N124: R70.Pin_0, LED79.cathode
  N125: R71.Pin_0, LED84.cathode
  N126: R72.Pin_0, LED85.cathode
  N127: R73.Pin_0, LED82.cathode
  N128: R74.Pin_0, LED71.cathode
  N129: R75.Pin_0, LED72.cathode
  N130: R76.Pin_0, LED73.cathode
  N131: R77.Pin_0, LED75.cathode
  N132: R78.Pin_0, LED77.cathode
  N133: R79.Pin_0, LED76.cathode
  N134: R80.Pin_1, LED94.cathode
  N135: R81.Pin_1, LED95.cathode
  N136: R82.Pin_1, LED61.cathode
  N137: R83.Pin_1, LED62.cathode
  N138: R84.Pin_1, LED63.cathode
  N139: R85.Pin_1, LED65.cathode
  N140: R86.Pin_1, LED68.cathode
  N141: R87.Pin_1, LED67.cathode
  N142: R88.Pin_1, LED64.cathode
  N143: R89.Pin_1, LED66.cathode
  N144: R90.Pin_0, LED90.cathode
  N145: R91.Pin_0, LED83.cathode
  N146: R92.Pin_0, LED81.cathode
  N147: LED74.cathode, R93.Pin_0

notes:
  FLAGS
  R0
  R1
  R2
  R3
  HLT
  MAR_s
  RAM_e
  RAM_s
  IR
  ALU2
  ALU1
  ALU0
  Ctmp_e
  IAR_e
  IAR_s
  TMP_s
  ACC_e
  FLAGS_s
  BUS1
  ACC_s
  JCOND
  R0_e
  R1_e
  R0_s
  R1_s
  IR_s
  R2_e
  R3_e
  R3_s
  R2_s
  IO_s
  IO_e
  IO_io
  IAR
