# Fritzing sketch jcscpu-hmc_first_half (saved by Fritzing 0.9.4)
breadboards: 7

parts:
  Part1 = Arduino Nano (Rev3.0) (ICSP)
  Part2 = Arduino Nano (Rev3.0) (ICSP)
  SW1 = DIP Switch 8 Position [package=dipswitch-08]
  U28 = 74HC595 [package="DIP16 [THT]"]
  U29 = 74HC595 [package="DIP16 [THT]"]
  R32 = Resistor [tolerance=±5% resistance=10k package="0402 [SMD]"]
  R33 = Resistor [tolerance=±5% resistance=10k package="0402 [SMD]"]
  R34 = Resistor [tolerance=±5% resistance=10k package="0402 [SMD]"]
  R35 = Resistor [tolerance=±5% resistance=10k package="0402 [SMD]"]
  R36 = Resistor [tolerance=±5% resistance=10k package="0402 [SMD]"]
  R37 = Resistor [tolerance=±5% resistance=10k package="0402 [SMD]"]
  R38 = Resistor [tolerance=±5% resistance=10k package="0402 [SMD]"]
  R5 = Resistor [tolerance=±5% resistance=1k package=THT]
  R7 = Resistor [tolerance=±5% resistance=1k package=THT]
  R6 = Resistor [tolerance=±5% resistance=1k package=THT]
  R4 = Resistor [tolerance=±5% resistance=1k package=THT]
  R3 = Resistor [tolerance=±5% resistance=1k package=THT]
  R2 = Resistor [tolerance=±5% resistance=1k package=THT]
  R8 = Resistor [tolerance=±5% resistance=1k package=THT]
  R1 = Resistor [tolerance=±5% resistance=1k package=THT]
  R39 = Resistor [tolerance=±5% resistance=10k package="0402 [SMD]"]
  SN74HC373 = IC, DIP package, 20 pins [chip_label=SN74HC373]
  SN74HC374 = IC, DIP package, 20 pins [chip_label=SN74HC373]
  SN74HC00 = IC, DIP package, 14 pins [chip_label=SN74HC00]
  SN74HC380 = IC, DIP package, 14 pins [chip_label=SN74HC00]
  R41 = Resistor [tolerance=±5% resistance=1k package=THT]
  R42 = Resistor [tolerance=±5% resistance=1k package=THT]
  R55 = Resistor [tolerance=±5% resistance=1k package=THT]
  R56 = Resistor [tolerance=±5% resistance=1k package=THT]
  R57 = Resistor [tolerance=±5% resistance=1k package=THT]
  R58 = Resistor [tolerance=±5% resistance=1k package=THT]
  R59 = Resistor [tolerance=±5% resistance=1k package=THT]
  R60 = Resistor [tolerance=±5% resistance=1k package=THT]
  R61 = Resistor [tolerance=±5% resistance=1k package=THT]
  R62 = Resistor [tolerance=±5% resistance=1k package=THT]
  R63 = Resistor [tolerance=±5% resistance=1k package=THT]
  R64 = Resistor [tolerance=±5% resistance=1k package=THT]
  R65 = Resistor [tolerance=±5% resistance=1k package=THT]
  R66 = Resistor [tolerance=±5% resistance=1k package=THT]
  R67 = Resistor [tolerance=±5% resistance=1k package=THT]
  R80 = Resistor [tolerance=±5% resistance=1k package=THT]
  R81 = Resistor [tolerance=±5% resistance=1k package=THT]
  R90 = Resistor [tolerance=±5% resistance=1k package=THT]
  LED86 = LED - 3mm [color="Yellow (595nm)" package="3 mm [THT]"]
  LED87 = LED - 3mm [color="Blue (505nm)" package="3 mm [THT]"]
  LED88 = LED - 3mm [color="Blue (505nm)" package="3 mm [THT]"]
  LED89 = LED - 3mm [color="Blue (505nm)" package="3 mm [THT]"]
  LED90 = LED - 3mm [color="Blue (505nm)" package="3 mm [THT]"]
  LED91 = LED - 3mm [color="Blue (505nm)" package="3 mm [THT]"]
  LED92 = LED - 3mm [color="Blue (505nm)" package="3 mm [THT]"]
  LED93 = LED - 3mm [color="Blue (505nm)" package="3 mm [THT]"]
  LED94 = LED - 3mm [color="Blue (505nm)" package="3 mm [THT]"]
  LED95 = LED - 3mm [color="Blue (505nm)" package="3 mm [THT]"]
  LED96 = LED - 3mm [color="Blue (505nm)" package="3 mm [THT]"]
  LED97 = LED - 3mm [color="Blue (505nm)" package="3 mm [THT]"]
  LED98 = LED - 3mm [color="Blue (505nm)" package="3 mm [THT]"]
  LED99 = LED - 3mm [color="Blue (505nm)" package="3 mm [THT]"]
  LED100 = LED - 3mm [color="Green (555nm)" package="3 mm [THT]"]
  LED101 = LED - 3mm [color="Green (555nm)" package="3 mm [THT]"]
  LED102 = LED - 3mm [color="Green (555nm)" package="3 mm [THT]"]
  LED103 = LED - 3mm [color="Red (633nm)" package="3 mm [THT]"]
  LED104 = LED - 3mm [color="Green (555nm)" package="3 mm [THT]"]
  LED105 = LED - 3mm [color="Green (555nm)" package="3 mm [THT]"]
  LED106 = LED - 3mm [color="Green (555nm)" package="3 mm [THT]"]
  LED107 = LED - 3mm [color="Green (555nm)" package="3 mm [THT]"]
  LED108 = LED - 3mm [color="Green (555nm)" package="3 mm [THT]"]
  LED109 = LED - 3mm [color="Green (555nm)" package="3 mm [THT]"]
  LED110 = LED - 3mm [color="Green (555nm)" package="3 mm [THT]"]
  LED111 = LED - 3mm [color="Green (555nm)" package="3 mm [THT]"]

nets:
  GND: Part1.GND, Part2.GND, U28.GND, U28.OE, U29.GND, U29.OE, R5.Pin_0, R7.Pin_0, R6.Pin_0, R4.Pin_0, R3.Pin_0, R2.Pin_0, R8.Pin_0, R1.Pin_0, SN74HC373.pin1, SN74HC374.pin1, SN74HC374.pin10, SN74HC00.pin7, SN74HC380.pin7, R41.Pin_0, R42.Pin_0, R55.Pin_1, R56.Pin_1, R57.Pin_1, R58.Pin_1, R59.Pin_1, R60.Pin_1, R61.Pin_1, R62.Pin_1, R63.Pin_1, R64.Pin_1, R65.Pin_1, R66.Pin_1, R67.Pin_1, R80.Pin_0, R81.Pin_0, R90.Pin_1
  N1: Part1.D2, U29.Q3, LED101.anode
  N2: Part1.D3, U29.Q2, LED100.anode
  N3: Part1.D4, U29.Q1, LED102.anode
  N4: Part1.D5, SW1.9, R38.Pin_0, SN74HC373.pin2, SN74HC373.pin3, LED111.anode
  N5: Part1.D6, SW1.10, R37.Pin_0, SN74HC373.pin4, SN74HC373.pin5, LED110.anode
  N6: Part1.D7, SW1.11, R39.Pin_0, SN74HC373.pin6, SN74HC373.pin7, LED108.anode
  N7: Part1.D8, SW1.12, R36.Pin_0, SN74HC373.pin8, SN74HC373.pin9, LED107.anode
  N8: Part1.D9, SW1.13, R34.Pin_0, LED109.anode
  N9: Part1.D10, SW1.14, R35.Pin_0, LED105.anode
  N10: Part1.D11/MOSI, SW1.15, R33.Pin_0, LED104.anode
  N11: Part1.D12/MISO, SW1.16, R32.Pin_0, LED106.anode
  5V: Part1.5V, Part2.5V, SW1.1, SW1.2, SW1.3, SW1.4, SW1.5, SW1.6, SW1.7, SW1.8, U28.MR, U28.VCC, U29.MR, U29.VCC, SN74HC374.pin20, SN74HC00.pin14, SN74HC380.pin14
  N12: Part1.A5, Part2.A5
  N13: Part1.A4, Part2.A4
  N14: Part1.A3, U29.Q0, LED103.anode
  N15: Part1.A2, U28.SH_CP, U29.SH_CP
  N16: Part1.A1, U28.ST_CP, U29.ST_CP
  N17: Part1.A0, U29.DS
  N18: Part2.D2, U28.Q3, LED89.anode
  N19: Part2.D5, U28.Q2, LED91.anode
  N20: Part2.D6, U28.Q1, LED90.anode
  N21: Part2.D7, U28.Q0, SN74HC380.pin2, SN74HC380.pin12, LED92.anode
  N22: Part2.D8, SN74HC00.pin11
  N23: Part2.D9, SN74HC374.pin8
  N24: Part2.D10, SN74HC374.pin7
  N25: Part2.D11/MOSI, SN74HC374.pin4
  N26: Part2.D12/MISO, SN74HC374.pin3
  N27: Part2.A2, U29.Q7, LED98.anode
  N28: Part2.A1, U29.Q6, LED97.anode
  N29: Part2.A0, U29.Q5, LED99.anode
  N30: U28.Q5, SN74HC00.pin2, LED88.anode
  N31: U28.Q6, SN74HC00.pin5, SN74HC00.pin6, LED86.anode
  N32: U28.DS, U29.Q7'
  N33: R7.Pin_1, LED110.cathode
  N34: R6.Pin_1, LED111.cathode
  N35: R4.Pin_1, LED107.cathode
  N36: R3.Pin_1, LED109.cathode
  N37: R2.Pin_1, LED105.cathode
  N38: R8.Pin_1, LED104.cathode
  N39: R1.Pin_1, LED106.cathode
  N40: SN74HC374.pin2, SN74HC380.pin1, LED95.anode
  N41: SN74HC374.pin5, LED93.anode
  N42: SN74HC374.pin6, LED94.anode
  N43: SN74HC374.pin9, LED96.anode
  N44: SN74HC374.pin11, LED87.anode
  N45: SN74HC00.pin1, SN74HC380.pin6, SN74HC380.pin9
  N46: SN74HC00.pin3, SN74HC00.pin12, SN74HC00.pin13
  N47: SN74HC380.pin3, SN74HC380.pin13
  N48: SN74HC380.pin4, SN74HC380.pin5, SN74HC380.pin8
  N49: SN74HC380.pin10, SN74HC380.pin11
  N50: R41.Pin_1, LED93.cathode
  N51: R42.Pin_1, LED96.cathode
  N52: R55.Pin_0, LED102.cathode
  N53: R56.Pin_0, LED103.cathode
  N54: R57.Pin_0, LED100.cathode
  N55: R58.Pin_0, LED101.cathode
  N56: R59.Pin_0, LED99.cathode
  N57: R60.Pin_0, LED98.cathode
  N58: R61.Pin_0, LED97.cathode
  N59: R62.Pin_0, LED87.cathode
  N60: R63.Pin_0, LED86.cathode
  N61: R64.Pin_0, LED88.cathode
  N62: R65.Pin_0, LED91.cathode
  N63: R66.Pin_0, LED92.cathode
  N64: R67.Pin_0, LED89.cathode
  N65: R80.Pin_1, LED94.cathode
  N66: R81.Pin_1, LED95.cathode
  N67: R90.Pin_0, LED90.cathode

notes:
  FLAGS
  HLT
  MAR_s
  RAM_e
  RAM_s
  ALU2
  ALU1
  ALU0
  Ctmp_e
  IAR_e
  TMP_s
  ACC_e
  FLAGS_s
  BUS1
  ACC_s
  R1_s
  IAR
