# Fritzing sketch jcscpu-hmc_second_half (saved by Fritzing 0.9.4)
breadboards: 14

parts:
  Part1 = Arduino Nano (Rev3.0) (ICSP)
  Part2 = Arduino Nano (Rev3.0) (ICSP)
  Part3 = Arduino Nano (Rev3.0) (ICSP)
  Part4 = Arduino Nano (Rev3.0) (ICSP)
  S1 = Pushbutton [package="[SMD]"]
  U30 = 74HC595 [package="DIP16 [THT]"]
  U31 = 74HC595 [package="DIP16 [THT]"]
  SN74HC376 = IC, DIP package, 20 pins [chip_label=SN74HC373]
  SN74HC377 = IC, DIP package, 20 pins [chip_label=SN74HC373]
  SN74HC378 = IC, DIP package, 20 pins [chip_label=SN74HC373]
  SN74HC379 = IC, DIP package, 20 pins [chip_label=SN74HC373]
  SN74HC381 = IC, DIP package, 20 pins [chip_label=SN74HC373]
  R44 = Resistor [tolerance=±5% resistance=1k package=THT]
  R45 = Resistor [tolerance=±5% resistance=1k package=THT]
  R47 = Resistor [tolerance=±5% resistance=1k package=THT]
  R48 = Resistor [tolerance=±5% resistance=1k package=THT]
  R49 = Resistor [tolerance=±5% resistance=1k package=THT]
  R50 = Resistor [tolerance=±5% resistance=1k package=THT]
  R51 = Resistor [tolerance=±5% resistance=1k package=THT]
  R52 = Resistor [tolerance=±5% resistance=1k package=THT]
  R53 = Resistor [tolerance=±5% resistance=10k package="0402 [SMD]"]
  SN74HC383 = IC, DIP package, 14 pins [chip_label=SN74HC00]
  SN74HC04 = IC, DIP package, 14 pins [chip_label=SN74HC08]
  SN74HC32 = IC, DIP package, 14 pins [chip_label=SN74HC32]
  R54 = Resistor [tolerance=±5% resistance=1k package=THT]
  SN74HC384 = IC, DIP package, 14 pins [chip_label=SN74HC00]
  R68 = Resistor [tolerance=±5% resistance=1k package=THT]
  R69 = Resistor [tolerance=±5% resistance=1k package=THT]
  R70 = Resistor [tolerance=±5% resistance=1k package=THT]
  R71 = Resistor [tolerance=±5% resistance=1k package=THT]
  R72 = Resistor [tolerance=±5% resistance=1k package=THT]
  R73 = Resistor [tolerance=±5% resistance=1k package=THT]
  R74 = Resistor [tolerance=±5% resistance=1k package=THT]
  R75 = Resistor [tolerance=±5% resistance=1k package=THT]
  R76 = Resistor [tolerance=±5% resistance=1k package=THT]
  R77 = Resistor [tolerance=±5% resistance=1k package=THT]
  R78 = Resistor [tolerance=±5% resistance=1k package=THT]
  R79 = Resistor [tolerance=±5% resistance=1k package=THT]
  LED60 = LED - 3mm [color="Red (633nm)" package="3 mm [THT]"]
  R82 = Resistor [tolerance=±5% resistance=1k package=THT]
  R83 = Resistor [tolerance=±5% resistance=1k package=THT]
  R84 = Resistor [tolerance=±5% resistance=1k package=THT]
  R85 = Resistor [tolerance=±5% resistance=1k package=THT]
  R86 = Resistor [tolerance=±5% resistance=1k package=THT]
  R87 = Resistor [tolerance=±5% resistance=1k package=THT]
  R88 = Resistor [tolerance=±5% resistance=1k package=THT]
  R89 = Resistor [tolerance=±5% resistance=1k package=THT]
  LED61 = LED - 3mm [color="Yellow (595nm)" package="3 mm [THT]"]
  LED62 = LED - 3mm [color="Yellow (595nm)" package="3 mm [THT]"]
  LED63 = LED - 3mm [color="Yellow (595nm)" package="3 mm [THT]"]
  LED64 = LED - 3mm [color="Yellow (595nm)" package="3 mm [THT]"]
  LED65 = LED - 3mm [color="Yellow (595nm)" package="3 mm [THT]"]
  LED66 = LED - 3mm [color="Yellow (595nm)" package="3 mm [THT]"]
  LED67 = LED - 3mm [color="Yellow (595nm)" package="3 mm [THT]"]
  LED68 = LED - 3mm [color="Yellow (595nm)" package="3 mm [THT]"]
  LED69 = LED - 3mm [color="Red (633nm)" package="3 mm [THT]"]
  LED70 = LED - 3mm [color="Red (633nm)" package="3 mm [THT]"]
  R91 = Resistor [tolerance=±5% resistance=1k package=THT]
  R92 = Resistor [tolerance=±5% resistance=1k package=THT]
  LED71 = LED - 3mm [color="Yellow (595nm)" package="3 mm [THT]"]
  LED72 = LED - 3mm [color="Yellow (595nm)" package="3 mm [THT]"]
  LED73 = LED - 3mm [color="Yellow (595nm)" package="3 mm [THT]"]
  LED74 = LED - 3mm [color="Yellow (595nm)" package="3 mm [THT]"]
  LED75 = LED - 3mm [color="Yellow (595nm)" package="3 mm [THT]"]
  LED76 = LED - 3mm [color="Yellow (595nm)" package="3 mm [THT]"]
  LED77 = LED - 3mm [color="Yellow (595nm)" package="3 mm [THT]"]
  R93 = Resistor [tolerance=±5% resistance=1k package=THT]
  LED78 = LED - 3mm [color="Yellow (595nm)" package="3 mm [THT]"]
  LED79 = LED - 3mm [color="Yellow (595nm)" package="3 mm [THT]"]
  LED80 = LED - 3mm [color="Yellow (595nm)" package="3 mm [THT]"]
  LED81 = LED - 3mm [color="Yellow (595nm)" package="3 mm [THT]"]
  LED82 = LED - 3mm [color="White (4500K)" package="3 mm [THT]"]
  LED83 = LED - 3mm [color="White (4500K)" package="3 mm [THT]"]
  LED84 = LED - 3mm [color="White (4500K)" package="3 mm [THT]"]
  LED85 = LED - 3mm [color="White (4500K)" package="3 mm [THT]"]
  LED112 = LED - 3mm [color="Red (633nm)" package="3 mm [THT]"]
  LED113 = LED - 3mm [color="Red (633nm)" package="3 mm [THT]"]
  LED114 = LED - 3mm [color="Red (633nm)" package="3 mm [THT]"]
  LED115 = LED - 3mm [color="Red (633nm)" package="3 mm [THT]"]
  LED116 = LED - 3mm [color="Red (633nm)" package="3 mm [THT]"]
  LED117 = LED - 3mm [color="Red (633nm)" package="3 mm [THT]"]

nets:
  N1: Part1.A5, Part2.A5, Part3.A5, Part4.A5
  N2: Part1.A4, Part2.A4, Part3.A4, Part4.A4
  GND: Part3.GND, Part4.GND, U30.OE, U31.OE, SN74HC383.pin7, SN74HC384.pin7
  N3: Part3.D3, LED60.anode
  N4: Part3.D4, S1.Pin_3, S1.Pin_4, R53.Pin_1
  N5: Part3.D5, LED70.anode
  N6: Part3.D6, LED117.anode
  N7: Part3.D7, LED115.anode
  N8: Part3.D8, LED116.anode
  N9: Part3.D9, LED113.anode
  N10: Part3.D10, LED114.anode
  N11: Part3.D11/MOSI, LED112.anode
  N12: Part3.D12/MISO, LED69.anode
  5V: Part3.5V, Part4.5V, U30.MR, U30.VCC, U31.MR, U31.VCC
  N13: Part3.A3, U30.Q3, LED82.anode
  N14: Part3.A2, U30.Q2, LED84.anode
  N15: Part3.A1, U30.Q1, LED83.anode
  N16: Part3.A0, U30.Q0, LED85.anode
  N17: Part4.D2, U31.Q2, LED75.anode
  N18: Part4.D3, SN74HC32.pin3
  N19: Part4.D5, SN74HC04.pin4, LED68.anode
  N20: Part4.D6, SN74HC04.pin1, LED67.anode
  N21: Part4.D7, SN74HC04.pin10, LED66.anode
  N22: Part4.D8, SN74HC04.pin13, LED65.anode
  N23: Part4.D9, LED63.anode
  N24: Part4.D10, LED64.anode
  N25: Part4.D11/MOSI, LED62.anode
  N26: Part4.D12/MISO, LED61.anode
  N27: Part4.A3, U31.Q1, LED77.anode
  N28: S1.Pin_1, S1.Pin_2, SN74HC377.pin20, SN74HC379.pin20, SN74HC04.pin14, SN74HC32.pin14
  N29: U30.Q4, SN74HC384.pin1, SN74HC384.pin2, LED81.anode
  N30: U30.Q5, SN74HC384.pin4, SN74HC384.pin5, LED79.anode
  N31: U30.Q6, LED80.anode
  N32: U30.Q7, LED78.anode
  GND_2: U30.GND, U31.GND, R68.Pin_1, R69.Pin_1, R70.Pin_1, R71.Pin_1, R72.Pin_1, R73.Pin_1, R74.Pin_1, R75.Pin_1, R76.Pin_1, R77.Pin_1, R78.Pin_1, R79.Pin_1, R91.Pin_1, R92.Pin_1, R93.Pin_1
  N33: U30.Q7', U31.DS
  N34: U30.SH_CP, U31.SH_CP
  N35: U30.ST_CP, U31.ST_CP
  N36: U31.Q3, SN74HC383.pin1, SN74HC383.pin2, LED76.anode
  N37: U31.Q4, SN74HC383.pin4, SN74HC383.pin5, LED74.anode
  N38: U31.Q5, SN74HC377.pin11, LED73.anode
  N39: U31.Q6, LED72.anode
  N40: U31.Q7, LED71.anode
  N41: SN74HC376.pin1, SN74HC384.pin6
  N42: SN74HC376.pin2, SN74HC376.pin3, SN74HC377.pin2, SN74HC377.pin3, SN74HC378.pin3, SN74HC379.pin2, SN74HC379.pin3, SN74HC381.pin2, SN74HC381.pin3
  N43: SN74HC376.pin4, SN74HC376.pin5, SN74HC377.pin4, SN74HC377.pin5, SN74HC378.pin4, SN74HC379.pin4, SN74HC379.pin5, SN74HC381.pin4, SN74HC381.pin5
  N44: SN74HC376.pin6, SN74HC376.pin7, SN74HC377.pin7, SN74HC378.pin7, SN74HC379.pin7, SN74HC381.pin6, SN74HC381.pin7
  N45: SN74HC376.pin8, SN74HC376.pin9, SN74HC377.pin8, SN74HC377.pin9, SN74HC378.pin8, SN74HC379.pin8, SN74HC379.pin9, SN74HC381.pin8, SN74HC381.pin9
  N46: SN74HC376.pin10, SN74HC378.pin1, SN74HC378.pin10, SN74HC379.pin10, SN74HC381.pin10, R44.Pin_0, R45.Pin_0, R47.Pin_0, R48.Pin_0, R49.Pin_0, R50.Pin_0, R51.Pin_0, R52.Pin_0, R53.Pin_0, R54.Pin_0, R82.Pin_0, R83.Pin_0, R84.Pin_0, R85.Pin_0, R86.Pin_0, R87.Pin_0, R88.Pin_0, R89.Pin_0
  N47: SN74HC377.pin1, SN74HC383.pin6
  N48: SN74HC377.pin12, SN74HC377.pin13, SN74HC379.pin12, SN74HC379.pin13
  N49: SN74HC377.pin14, SN74HC377.pin15, SN74HC379.pin14, SN74HC379.pin15
  N50: SN74HC377.pin16, SN74HC377.pin17, SN74HC379.pin16, SN74HC379.pin17
  N51: SN74HC377.pin18, SN74HC377.pin19, SN74HC379.pin18, SN74HC379.pin19
  N52: SN74HC379.pin1, SN74HC383.pin3
  N53: SN74HC381.pin1, SN74HC384.pin3
  N54: R44.Pin_1, LED70.cathode
  N55: R45.Pin_1, LED117.cathode
  N56: R47.Pin_1, LED116.cathode
  N57: R48.Pin_1, LED113.cathode
  N58: R49.Pin_1, LED115.cathode
  N59: R50.Pin_1, LED114.cathode
  N60: R51.Pin_1, LED112.cathode
  N61: R52.Pin_1, LED60.cathode
  N62: SN74HC383.pin14, SN74HC384.pin14
  N63: SN74HC04.pin3, SN74HC32.pin4
  N64: SN74HC04.pin6, SN74HC32.pin5
  N65: SN74HC04.pin7, SN74HC32.pin7
  N66: SN74HC04.pin8, SN74HC32.pin11
  N67: SN74HC04.pin11, SN74HC32.pin9
  N68: SN74HC32.pin1, SN74HC32.pin8
  N69: SN74HC32.pin2, SN74HC32.pin6
  N70: R54.Pin_1, LED69.cathode
  N71: R68.Pin_0, LED78.cathode
  N72: R69.Pin_0, LED80.cathode
  N73: R70.Pin_0, LED79.cathode
  N74: R71.Pin_0, LED84.cathode
  N75: R72.Pin_0, LED85.cathode
  N76: R73.Pin_0, LED82.cathode
  N77: R74.Pin_0, LED71.cathode
  N78: R75.Pin_0, LED72.cathode
  N79: R76.Pin_0, LED73.cathode
  N80: R77.Pin_0, LED75.cathode
  N81: R78.Pin_0, LED77.cathode
  N82: R79.Pin_0, LED76.cathode
  N83: R82.Pin_1, LED61.cathode
  N84: R83.Pin_1, LED62.cathode
  N85: R84.Pin_1, LED63.cathode
  N86: R85.Pin_1, LED65.cathode
  N87: R86.Pin_1, LED68.cathode
  N88: R87.Pin_1, LED67.cathode
  N89: R88.Pin_1, LED64.cathode
  N90: R89.Pin_1, LED66.cathode
  N91: R91.Pin_0, LED83.cathode
  N92: R92.Pin_0, LED81.cathode
  N93: LED74.cathode, R93.Pin_0

notes:
  R0
  R1
  R2
  R3
  IR
  IAR_s
  JCOND
  R0_e
  R1_e
  R0_s
  R1_s
  IR_s
  R2_e
  R3_e
  R3_s
  R2_s
  IO_s
  IO_e
  IO_io
